// Logisim project xComputer.circ as structural Verilog: 15 circuits, main circuit main
module main (
  input  RESET
);

  wire alu_1_to_flag, and_1_out, clock_1_out, control_circuit_1_decrement_ac, control_circuit_1_increment_ac,
       control_circuit_1_increment_pc, control_circuit_1_load_ac_from_alu, control_circuit_1_load_ac_from_ir,
       control_circuit_1_load_ac_from_memory, control_circuit_1_load_addr_from_ir,
       control_circuit_1_load_addr_from_pc, control_circuit_1_load_addr_from_y,
       control_circuit_1_load_data_into_memory, control_circuit_1_load_flag_from_alu,
       control_circuit_1_load_ir_from_memory, control_circuit_1_load_pc_from_ir,
       control_circuit_1_load_pc_from_memory, control_circuit_1_load_x_from_ac,
       control_circuit_1_load_y_from_ir, control_circuit_1_load_y_from_memory, control_circuit_1_select_add,
       control_circuit_1_select_and, control_circuit_1_select_not, control_circuit_1_select_or,
       control_circuit_1_select_shift_left, control_circuit_1_select_shift_right,
       control_circuit_1_select_subtract, control_circuit_1_set_count_to_zero, control_circuit_1_stop_clock,
       flag_register_1_out_3, not_1_out, not_2_out, or_1_out;
  wire [3:0] counter_1_q;
  wire [5:0] instruction_register_1_instruction;
  wire [9:0] address_register_1_out_7, instruction_register_1_data, program_counter_1_out_8;
  wire [15:0] accumulator_1_out_10, alu_1_to_ac, ram_1_data, x_register_1_out_3, y_register_1_out_5;

  Clock clock_1 (.out(clock_1_out));
  Control_Circuit control_circuit_1 (
    .From_COUNT(counter_1_q), .From_IR(instruction_register_1_instruction), .From_AC(accumulator_1_out_10),
    .From_Flag(flag_register_1_out_3), .Stop_Clock(control_circuit_1_stop_clock),
    .Set_Count_to_Zero(control_circuit_1_set_count_to_zero),
    .Load_Y_from_Memory(control_circuit_1_load_y_from_memory),
    .Load_Y_from_IR(control_circuit_1_load_y_from_ir), .Load_X_from_AC(control_circuit_1_load_x_from_ac),
    .Select_Add(control_circuit_1_select_add), .Select_Subtract(control_circuit_1_select_subtract),
    .Select_Shift_left(control_circuit_1_select_shift_left),
    .Select_Shift_right(control_circuit_1_select_shift_right), .Select_AND(control_circuit_1_select_and),
    .Select_OR(control_circuit_1_select_or), .Select_NOT(control_circuit_1_select_not),
    .Load_Flag_from_ALU(control_circuit_1_load_flag_from_alu),
    .Load_AC_from_ALU(control_circuit_1_load_ac_from_alu),
    .Load_AC_from_Memory(control_circuit_1_load_ac_from_memory),
    .Load_AC_from_IR(control_circuit_1_load_ac_from_ir), .Increment_AC(control_circuit_1_increment_ac),
    .Decrement_AC(control_circuit_1_decrement_ac),
    .Load_IR_from_Memory(control_circuit_1_load_ir_from_memory),
    .Load_PC_from_IR(control_circuit_1_load_pc_from_ir),
    .Load_PC_from_Memory(control_circuit_1_load_pc_from_memory),
    .Increment_PC(control_circuit_1_increment_pc), .Load_ADDR_from_Y(control_circuit_1_load_addr_from_y),
    .Load_ADDR_from_PC(control_circuit_1_load_addr_from_pc),
    .Load_ADDR_from_IR(control_circuit_1_load_addr_from_ir),
    .Load_DATA_into_Memory(control_circuit_1_load_data_into_memory));
  not not_1 (not_1_out, control_circuit_1_stop_clock);
  and and_1 (and_1_out, clock_1_out, not_1_out);
  Counter #(.width(4), .max('hf)) counter_1 (
    .Q(counter_1_q), .clk(and_1_out), .clr(or_1_out));  // open: load, D, count, carry
  // Probe on counter_1_q
  or or_1 (or_1_out, RESET, control_circuit_1_set_count_to_zero);
  X_Register x_register_1 (
    .Load_X_from_AC(control_circuit_1_load_x_from_ac), .From_AC(accumulator_1_out_10),
    .out_3(x_register_1_out_3));
  // Probe on x_register_1_out_3
  Y_Register y_register_1 (
    .Load_Y_from_Memory(control_circuit_1_load_y_from_memory),
    .Load_Y_from_IR(control_circuit_1_load_y_from_ir), .From_Memory(ram_1_data),
    .From_IR(instruction_register_1_data), .out_5(y_register_1_out_5));
  ALU alu_1 (
    .Select_Add(control_circuit_1_select_add), .Select_Subtract(control_circuit_1_select_subtract),
    .Select_Shift_Left(control_circuit_1_select_shift_left),
    .Select_Shift_Right(control_circuit_1_select_shift_right), .Select_AND(control_circuit_1_select_and),
    .Select_OR(control_circuit_1_select_or), .Select_NOT(control_circuit_1_select_not),
    .From_X(x_register_1_out_3), .From_Y(y_register_1_out_5), .To_Flag(alu_1_to_flag), .To_AC(alu_1_to_ac));
  Flag_Register flag_register_1 (
    .Load_Flag_from_ALU(control_circuit_1_load_flag_from_alu), .From_ALU(alu_1_to_flag),
    .out_3(flag_register_1_out_3));
  // Probe on accumulator_1_out_10
  // Probe on y_register_1_out_5
  // Probe on alu_1_to_ac
  Accumulator accumulator_1 (
    .Load_AC_from_ALU(control_circuit_1_load_ac_from_alu),
    .Load_AC_from_IR(control_circuit_1_load_ac_from_ir),
    .Load_AC_from_Memory(control_circuit_1_load_ac_from_memory),
    .Increment_AC(control_circuit_1_increment_ac), .Decrement_AC(control_circuit_1_decrement_ac),
    .from_ALU(alu_1_to_ac), .from_IR(instruction_register_1_data), .from_Memory(ram_1_data),
    .out_10(accumulator_1_out_10), .CLOCK(counter_1_q));
  Program_Counter program_counter_1 (
    .Load_PC_from_IR(control_circuit_1_load_pc_from_ir),
    .Load_PC_from_Memory(control_circuit_1_load_pc_from_memory),
    .Increment_PC(control_circuit_1_increment_pc), .From_IR(instruction_register_1_data),
    .From_Memory(ram_1_data), .out_8(program_counter_1_out_8), .RESET(RESET), .count(counter_1_q));
  // Probe on program_counter_1_out_8
  Address_Register address_register_1 (
    .Load_ADDR_from_Y(control_circuit_1_load_addr_from_y),
    .Load_ADDR_from_PC(control_circuit_1_load_addr_from_pc),
    .Load_ADDR_from_IR(control_circuit_1_load_addr_from_ir), .From_Y(y_register_1_out_5),
    .From_PC(program_counter_1_out_8), .From_IR(instruction_register_1_data), .out_7(address_register_1_out_7));
  // Probe on address_register_1_out_7
  // Probe on address_register_1_out_7
  Instruction_Register instruction_register_1 (
    .Load_IR_from_Memory(control_circuit_1_load_ir_from_memory), .in_1(ram_1_data),
    .Instruction(instruction_register_1_instruction), .Data(instruction_register_1_data));
  // Probe on instruction_register_1_data
  // Probe on instruction_register_1_instruction
  not not_2 (not_2_out, control_circuit_1_load_data_into_memory);
  RAM #(.addrWidth(10), .dataWidth(16), .bus("asynch")) ram_1 (
    .addr(address_register_1_out_7), .data(ram_1_data), .ld(not_2_out));  // open: sel, clr
  assign ram_1_data = control_circuit_1_load_data_into_memory ? accumulator_1_out_10 : 16'bz;  // Controlled_Buffer controlled_buffer_1

  // Notes on the sheet:
  //   CLOCK
  //   from COUNT
  //   from IR
  //   from AC
  //   from
  //   Flag
  //   Stop Clock
  //   Set COUNT To Zero
  //   Load Y from Memory
  //   Load Y from IR
  //   Load X from AC
  //   Select Add
  //   Select Subtract
  //   Select Shift Left
  //   Select Shift Right
  //   Select AND
  //   Select OR
  //   Select NOT
  //   Load Flad from ALU
  //   Load AC from ALU
  //   Load AC from Memory
  //   Load AC from IR
  //   Increment AC
  //   Decrement AC
  //   Load IR from Memory
  //   Load PC from IR
  //   Load PC from Memory
  //   Increment PC
  //   Load ADDR from Y
  //   Load ADDR from PC
  //   Load ADDR from IR
  //   Load Data into Memory
  //   COUNT
  //   Instruction
  //   (binary)
  //   address
  //   address
  //   (hex)
  //   RAM (Main Memory)
endmodule

// AC
module Accumulator (
  input  [15:0] from_ALU,
  input  [9:0] from_IR,
  input  [15:0] from_Memory,
  input  Load_AC_from_ALU,
  input  Load_AC_from_IR,
  input  Load_AC_from_Memory,
  input  Increment_AC,
  input  Decrement_AC,
  input  [3:0] CLOCK,
  output [15:0] out_10
);

  wire and_1_out, not_1_out, not_2_out, not_3_out, or_1_out, or_2_out;
  wire [1:0] or_3_out;
  wire [15:0] adder_1_out, bit_extender_1_out, multiplexer_1_out, multiplexer_2_out, register_1_q,
       register_2_q, subtractor_1_out;

  or or_1 (or_1_out, Increment_AC, Decrement_AC);
  Adder #(.width(16)) adder_1 (.a(out_10), .b(16'h1), .out(adder_1_out));  // open: cin, cout
  Subtractor #(.width(16)) subtractor_1 (.a(out_10), .b(16'h1), .out(subtractor_1_out));  // open: bin, bout
  Register #(.width(16), .trigger("high")) register_1 (
    .D(adder_1_out), .Q(register_1_q), .clk(and_1_out));  // open: en, clr
  Register #(.width(16), .trigger("high")) register_2 (
    .D(subtractor_1_out), .Q(register_2_q), .clk(and_1_out));  // open: en, clr
  Multiplexer #(.width(16)) multiplexer_1 (
    .in0(register_1_q), .in1(register_2_q), .out(multiplexer_1_out), .sel(Decrement_AC));  // open: en
  assign bit_extender_1_out = {{6{1'b0}}, from_IR};  // Bit_Extender bit_extender_1
  or or_2 (or_2_out, Load_AC_from_ALU, Load_AC_from_IR, Load_AC_from_Memory, or_1_out);
  and and_1 (and_1_out, not_1_out, CLOCK[1], not_2_out, not_3_out);
  or or_3 (or_3_out[0], Load_AC_from_IR, or_1_out);
  or or_4 (or_3_out[1], or_1_out, Load_AC_from_Memory);
  Multiplexer #(.select(2), .width(16)) multiplexer_2 (
    .in0(from_ALU), .in1(bit_extender_1_out), .in2(from_Memory), .in3(multiplexer_1_out),
    .out(multiplexer_2_out), .sel(or_3_out));  // open: en
  not not_1 (not_1_out, CLOCK[0]);
  not not_2 (not_2_out, CLOCK[2]);
  not not_3 (not_3_out, CLOCK[3]);
  Register #(.width(16), .trigger("high")) register_3 (
    .D(multiplexer_2_out), .Q(out_10), .clk(or_2_out));  // open: en, clr
endmodule

// Count
module COUNT_Register (
  input  [2:0] Clock_count,
  input  Set_COUNT_to_Zero,
  input  RESET,
  output [3:0] out_4
);

  wire and_1_out, and_2_out, and_3_out, and_4_out, not_1_out, not_2_out, not_3_out, not_4_out, not_5_out,
       or_1_out;
  wire [3:0] adder_1_out, register_1_q;

  not not_1 (not_1_out, Clock_count[1]);
  not not_2 (not_2_out, Clock_count[2]);
  not not_3 (not_3_out, Clock_count[2]);
  not not_4 (not_4_out, Clock_count[0]);
  and and_1 (and_1_out, Clock_count[0], not_1_out, not_2_out);
  not not_5 (not_5_out, Clock_count[2]);
  and and_2 (and_2_out, not_3_out, Clock_count[1], not_4_out);
  and and_3 (and_3_out, and_2_out, Set_COUNT_to_Zero);
  Adder #(.width(4)) adder_1 (.a(out_4), .b(4'b0001), .out(adder_1_out));  // open: cin, cout
  and and_4 (and_4_out, Clock_count[0], Clock_count[1], not_5_out);
  or or_1 (or_1_out, and_3_out, RESET);
  Register #(.width(4), .trigger("high")) register_1 (
    .D(adder_1_out), .Q(register_1_q), .clk(and_1_out), .clr(or_1_out));  // open: en
  Register #(.width(4), .trigger("high")) register_2 (
    .D(register_1_q), .Q(out_4), .clk(and_4_out), .clr(or_1_out));  // open: en
endmodule

// ADDR
module Address_Register (
  input  [15:0] From_Y,
  input  [9:0] From_PC,
  input  [9:0] From_IR,
  input  Load_ADDR_from_Y,
  input  Load_ADDR_from_PC,
  input  Load_ADDR_from_IR,
  output [9:0] out_7
);

  wire or_1_out;
  wire [9:0] bit_extender_1_out, multiplexer_1_out;

  Bit_Extender #(.in_width(16), .out_width(10)) bit_extender_1 (.in(From_Y), .out(bit_extender_1_out));
  Multiplexer #(.select(2), .width(10)) multiplexer_1 (
    .in0(bit_extender_1_out), .in1(From_PC), .in2(From_IR), .out(multiplexer_1_out),
    .sel({Load_ADDR_from_IR, Load_ADDR_from_PC}));  // open: in3, en
  Register #(.width(10), .trigger("high")) register_1 (
    .D(multiplexer_1_out), .Q(out_7), .clk(or_1_out));  // open: en, clr
  or or_1 (or_1_out, Load_ADDR_from_Y, Load_ADDR_from_PC, Load_ADDR_from_IR);
endmodule

// IR
module Instruction_Register (
  input  [15:0] in_1,
  input  Load_IR_from_Memory,
  output [5:0] Instruction,
  output [9:0] Data
);

  Register #(.width(16)) register_1 (.D(in_1), .Q({Instruction, Data}), .clk(Load_IR_from_Memory));  // open: en, clr
endmodule

// PC
module Program_Counter (
  input  [9:0] From_IR,
  input  [15:0] From_Memory,
  input  RESET,
  input  Load_PC_from_IR,
  input  [3:0] count,
  input  Load_PC_from_Memory,
  input  Increment_PC,
  output [9:0] out_8
);

  wire and_1_out, not_1_out, not_2_out, not_3_out, or_1_out;
  wire [9:0] adder_1_out, bit_extender_1_out, multiplexer_1_out, register_1_q;

  Adder #(.width(10)) adder_1 (.a(out_8), .b(10'h1), .out(adder_1_out));  // open: cin, cout
  Bit_Extender #(.in_width(16), .out_width(10)) bit_extender_1 (.in(From_Memory), .out(bit_extender_1_out));
  Register #(.width(10), .trigger("high")) register_1 (
    .D(adder_1_out), .Q(register_1_q), .clk(and_1_out), .clr(RESET));  // open: en
  Multiplexer #(.select(2), .width(10)) multiplexer_1 (
    .in0(From_IR), .in1(bit_extender_1_out), .in2(register_1_q), .out(multiplexer_1_out),
    .sel({Increment_PC, Load_PC_from_Memory}));  // open: in3, en
  or or_1 (or_1_out, Load_PC_from_IR, Load_PC_from_Memory, Increment_PC);
  Register #(.width(10), .trigger("high")) register_2 (
    .D(multiplexer_1_out), .Q(out_8), .clk(or_1_out), .clr(RESET));  // open: en
  and and_1 (and_1_out, count[0], not_1_out, not_2_out, not_3_out);
  not not_1 (not_1_out, count[1]);
  not not_2 (not_2_out, count[2]);
  not not_3 (not_3_out, count[3]);
endmodule

// X
module X_Register (
  input  [15:0] From_AC,
  input  Load_X_from_AC,
  output [15:0] out_3
);

  Register #(.width(16), .trigger("high")) register_1 (.D(From_AC), .Q(out_3), .clk(Load_X_from_AC));  // open: en, clr
endmodule

// Y
module Y_Register (
  input  [15:0] From_Memory,
  input  [9:0] From_IR,
  input  Load_Y_from_Memory,
  input  Load_Y_from_IR,
  output [15:0] out_5
);

  wire or_1_out;
  wire [15:0] bit_extender_1_out, multiplexer_1_out;

  assign bit_extender_1_out = {{6{1'b0}}, From_IR};  // Bit_Extender bit_extender_1
  Multiplexer #(.width(16)) multiplexer_1 (
    .in0(From_Memory), .in1(bit_extender_1_out), .out(multiplexer_1_out), .sel(Load_Y_from_IR));  // open: en
  or or_1 (or_1_out, Load_Y_from_Memory, Load_Y_from_IR);
  Register #(.width(16), .trigger("high")) register_1 (
    .D(multiplexer_1_out), .Q(out_5), .clk(or_1_out));  // open: en, clr
endmodule

// Flag
module Flag_Register (
  input  From_ALU,
  input  Load_Flag_from_ALU,
  output out_3
);

  Register #(.width(1), .trigger("high")) register_1 (
    .D(From_ALU), .Q(out_3), .clk(Load_Flag_from_ALU));  // open: en, clr
endmodule

module ALU (
  input  [15:0] From_X,
  input  [15:0] From_Y,
  input  Select_Add,
  input  Select_Subtract,
  input  Select_Shift_Left,
  input  Select_Shift_Right,
  input  Select_AND,
  input  Select_OR,
  input  Select_NOT,
  output [15:0] To_AC,
  output To_Flag
);

  wire adder_1_cout, and_1_out, and_2_out, and_3_out, and_4_out, subtractor_1_bout;
  wire [2:0] or_3_out;
  wire [15:0] adder_1_out, and_5_out, not_1_out, or_2_out, shifter_1_out, shifter_2_out, subtractor_1_out;

  Adder #(.width(16)) adder_1 (.a(From_X), .b(From_Y), .out(adder_1_out), .cout(adder_1_cout));  // open: cin
  Subtractor #(.width(16)) subtractor_1 (
    .a(From_X), .b(From_Y), .out(subtractor_1_out), .bout(subtractor_1_bout));  // open: bin
  Shifter #(.width(16)) shifter_1 (.in(From_X), .\dist (4'b0001), .out(shifter_1_out));
  and and_1 (and_1_out, subtractor_1_bout, Select_Subtract);
  and and_2 (and_2_out, adder_1_cout, Select_Add);
  or or_1 (To_Flag, and_2_out, and_1_out, and_4_out, and_3_out);
  Shifter #(.width(16), .shift("lr")) shifter_2 (.in(From_X), .\dist (4'b0001), .out(shifter_2_out));
  and and_3 (and_3_out, From_X[0], Select_Shift_Right);
  and and_4 (and_4_out, From_X[15], Select_Shift_Left);
  assign and_5_out = From_X & From_Y;  // AND_Gate and_5, 16 bits wide
  assign or_2_out = From_X | From_Y;  // OR_Gate or_2, 16 bits wide
  assign not_1_out = ~From_X;  // NOT_Gate not_1, 16 bits wide
  or or_3 (or_3_out[0], Select_Subtract, Select_Shift_Right, Select_OR);
  or or_4 (or_3_out[1], Select_Shift_Left, Select_Shift_Right, Select_NOT);
  or or_5 (or_3_out[2], Select_AND, Select_OR, Select_NOT);
  Multiplexer #(.select(3), .width(16)) multiplexer_1 (
    .in0(adder_1_out), .in1(subtractor_1_out), .in2(shifter_1_out), .in3(shifter_2_out), .in4(and_5_out),
    .in5(or_2_out), .in6(not_1_out), .out(To_AC), .sel(or_3_out));  // open: in7, en
endmodule

module Control_Circuit (
  input  [3:0] From_COUNT,
  input  [5:0] From_IR,
  input  [15:0] From_AC,
  input  From_Flag,
  output Stop_Clock,
  output Set_Count_to_Zero,
  output Load_Y_from_Memory,
  output Load_Y_from_IR,
  output Load_X_from_AC,
  output Select_Add,
  output Select_Subtract,
  output Select_Shift_left,
  output Select_Shift_right,
  output Select_AND,
  output Select_OR,
  output Select_NOT,
  output Load_Flag_from_ALU,
  output Load_AC_from_ALU,
  output Load_AC_from_Memory,
  output Load_AC_from_IR,
  output Increment_AC,
  output Decrement_AC,
  output Load_IR_from_Memory,
  output Load_PC_from_IR,
  output Load_PC_from_Memory,
  output Increment_PC,
  output Load_ADDR_from_Y,
  output Load_ADDR_from_PC,
  output Load_ADDR_from_IR,
  output Load_DATA_into_Memory
);

  wire and_2_out, and_3_out, and_7_out, and_8_out, control_for_count_0_1_set_count_to_zero,
       control_for_jumps_1_load_addr_from_ir_for_jump, control_for_jumps_1_set_count_0__jump_not_taken,
       control_for_operators_1_load_addr_from_ir_for_binop,
       control_for_operators_1_load_addr_from_y_for_binop, control_for_operators_1_load_y_from_mem_for_binop,
       control_for_sto_lod_1_load_addr_from_ir_for_sto_lod,
       control_for_sto_lod_1_load_addr_from_y_for_sto_lod, control_for_sto_lod_1_load_y_from_mem_for_sto_lod,
       decoder_1_out4, decoder_1_out5, decoder_1_out6, decoder_1_out7, decoder_2_out4, decoder_2_out5,
       decoder_2_out6, decoder_2_out7, decoder_2_out8, decoder_2_out9, decoder_2_out10, decoder_2_out11,
       decoder_3_out0, decoder_3_out1, decoder_3_out2, or_1_out, or_2_out;

  Decoder #(.select(4)) decoder_1 (
    .out1(Load_ADDR_from_PC), .out2(Load_IR_from_Memory), .out3(Increment_PC), .out4(decoder_1_out4),
    .out5(decoder_1_out5), .out6(decoder_1_out6), .out7(decoder_1_out7), .sel(From_COUNT));  // open: out0, out8, out9, out10, out11, out12, out13, out14, out15, en
  Decoder #(.select(4)) decoder_2 (
    .out4(decoder_2_out4), .out5(decoder_2_out5), .out6(decoder_2_out6), .out7(decoder_2_out7),
    .out8(decoder_2_out8), .out9(decoder_2_out9), .out10(decoder_2_out10), .out11(decoder_2_out11),
    .sel(From_IR[3:0]));  // open: out0, out1, out2, out3, out12, out13, out14, out15, en
  Decoder #(.select(2)) decoder_3 (
    .out0(decoder_3_out0), .out1(decoder_3_out1), .out2(decoder_3_out2), .sel(From_IR[5:4]));  // open: out3, en
  and and_1 (Stop_Clock, decoder_1_out4, decoder_2_out11, decoder_3_out0);
  or or_1 (or_1_out, decoder_1_out5, decoder_1_out6);
  and and_2 (and_2_out, decoder_3_out2, decoder_1_out7);
  or or_2 (or_2_out, and_2_out, and_3_out);
  and and_3 (and_3_out, decoder_3_out0, decoder_1_out5);
  and and_4 (Select_Shift_left, decoder_2_out5, decoder_3_out0, or_1_out);
  and and_5 (Select_Shift_right, decoder_2_out6, decoder_3_out0, or_1_out);
  and and_6 (Select_NOT, decoder_2_out4, decoder_3_out0, or_1_out);
  and and_7 (and_7_out, decoder_3_out0, decoder_2_out9, decoder_1_out5);
  and and_8 (and_8_out, decoder_3_out2, decoder_2_out9, decoder_1_out7);
  and and_9 (Increment_AC, decoder_2_out7, decoder_1_out4, decoder_3_out0);
  and and_10 (Decrement_AC, decoder_2_out8, decoder_1_out4, decoder_3_out0);
  and and_11 (Load_DATA_into_Memory, decoder_2_out10, or_2_out);
  or or_3 (Load_AC_from_Memory, and_7_out, and_8_out);
  and and_12 (Load_AC_from_IR, decoder_2_out9, decoder_1_out4, decoder_3_out1);
  Control_for_Count_0 control_for_count_0_1 (
    .count(From_COUNT), .Instruction(From_IR[3:0]), .Mode(From_IR[5:4]),
    .Set_Count_to_Zero(control_for_count_0_1_set_count_to_zero));
  Control_for_Sto_Lod control_for_sto_lod_1 (
    .count(From_COUNT), .Instruction(From_IR[3:0]), .Mode(From_IR[5:4]),
    .Load_Y_from_Mem_for_Sto_Lod(control_for_sto_lod_1_load_y_from_mem_for_sto_lod),
    .Load_ADDR_from_Y_for_Sto_Lod(control_for_sto_lod_1_load_addr_from_y_for_sto_lod),
    .Load_ADDR_from_IR_for_Sto_Lod(control_for_sto_lod_1_load_addr_from_ir_for_sto_lod));
  Control_for_Operators control_for_operators_1 (
    .count(From_COUNT), .Instruction(From_IR[3:0]), .Mode(From_IR[5:4]), .Select_ADD(Select_Add),
    .Select_Subtract(Select_Subtract), .Select_AND(Select_AND), .Select_OR(Select_OR),
    .Load_Y_from_Mem_for_BinOp(control_for_operators_1_load_y_from_mem_for_binop),
    .Loady_Y_from_IR(Load_Y_from_IR), .Load_X_from_AC(Load_X_from_AC),
    .Load_Flag_from_ALU(Load_Flag_from_ALU), .Load_AC_from_ALU(Load_AC_from_ALU),
    .Load_ADDR_from_Y_for_BinOp(control_for_operators_1_load_addr_from_y_for_binop),
    .Load_ADDR_from_IR_for_BinOp(control_for_operators_1_load_addr_from_ir_for_binop));
  Control_for_Jumps control_for_jumps_1 (
    .count(From_COUNT), .Instruction(From_IR[3:0]), .Mode(From_IR[5:4]), .AC(From_AC), .Flag(From_Flag),
    .Load_PC_from_IR(Load_PC_from_IR), .Load_PC_from_Memory(Load_PC_from_Memory),
    .Load_ADDR_from_IR_for_Jump(control_for_jumps_1_load_addr_from_ir_for_jump),
    .set_count_0__jump_not_taken(control_for_jumps_1_set_count_0__jump_not_taken));
  or or_4 (Set_Count_to_Zero, control_for_count_0_1_set_count_to_zero, control_for_jumps_1_set_count_0__jump_not_taken);
  or or_5 (Load_Y_from_Memory, control_for_operators_1_load_y_from_mem_for_binop, control_for_sto_lod_1_load_y_from_mem_for_sto_lod);
  or or_6 (Load_ADDR_from_Y, control_for_operators_1_load_addr_from_y_for_binop, control_for_sto_lod_1_load_addr_from_y_for_sto_lod);
  or or_7 (Load_ADDR_from_IR, control_for_sto_lod_1_load_addr_from_ir_for_sto_lod, control_for_operators_1_load_addr_from_ir_for_binop, control_for_jumps_1_load_addr_from_ir_for_jump);

  // Notes on the sheet:
  //   Count (0 - 10)
  //   Instruction (0 - 15)
  //   Mode (0 - 2)
  //   Lod/Sto Control
  //   Operator Control
  //   Jump Control
endmodule

module Control_for_Jumps (
  input  [3:0] count,
  input  [3:0] Instruction,
  input  [1:0] Mode,
  input  [15:0] AC,
  input  Flag,
  output Load_PC_from_IR,
  output Load_PC_from_Memory,
  output Load_ADDR_from_IR_for_Jump,
  output set_count_0__jump_not_taken
);

  wire and_1_out, and_2_out, and_3_out, comparator_1_eq, comparator_1_lt, decoder_1_out4, decoder_1_out5,
       decoder_2_out12, decoder_2_out13, decoder_2_out14, decoder_2_out15, decoder_3_out0, decoder_3_out2,
       not_1_out, or_1_out, or_2_out;

  Decoder #(.select(4)) decoder_1 (
    .out4(decoder_1_out4), .out5(decoder_1_out5), .sel(count));  // open: out0, out1, out2, out3, out6, out7, out8, out9, out10, out11, out12, out13, out14, out15, en
  Decoder #(.select(4)) decoder_2 (
    .out12(decoder_2_out12), .out13(decoder_2_out13), .out14(decoder_2_out14), .out15(decoder_2_out15),
    .sel(Instruction));  // open: out0, out1, out2, out3, out4, out5, out6, out7, out8, out9, out10, out11, en
  Decoder #(.select(2)) decoder_3 (.out0(decoder_3_out0), .out2(decoder_3_out2), .sel(Mode));  // open: out1, out3, en
  Comparator #(.width(16)) comparator_1 (
    .a(AC), .b({16{1'b0}}), .eq(comparator_1_eq), .lt(comparator_1_lt));  // open: gt
  and and_1 (and_1_out, decoder_2_out13, comparator_1_eq);
  and and_2 (and_2_out, decoder_2_out14, comparator_1_lt);
  and and_3 (and_3_out, decoder_2_out15, Flag);
  or or_1 (or_1_out, decoder_2_out12, and_1_out, and_2_out, and_3_out);
  and and_4 (Load_PC_from_IR, decoder_1_out4, decoder_3_out0, or_1_out);
  and and_5 (Load_PC_from_Memory, decoder_1_out5, decoder_3_out2, or_1_out);
  and and_6 (Load_ADDR_from_IR_for_Jump, decoder_1_out4, decoder_3_out2, or_1_out);
  not not_1 (not_1_out, or_1_out);
  or or_2 (or_2_out, decoder_2_out12, decoder_2_out13, decoder_2_out14, decoder_2_out15);
  and and_7 (set_count_0__jump_not_taken, not_1_out, or_2_out, decoder_1_out4);
endmodule

module Control_for_Operators (
  input  [3:0] count,
  input  [3:0] Instruction,
  input  [1:0] Mode,
  output Select_ADD,
  output Select_Subtract,
  output Select_AND,
  output Select_OR,
  output Load_Y_from_Mem_for_BinOp,
  output Loady_Y_from_IR,
  output Load_X_from_AC,
  output Load_Flag_from_ALU,
  output Load_AC_from_ALU,
  output Load_ADDR_from_Y_for_BinOp,
  output Load_ADDR_from_IR_for_BinOp
);

  wire and_1_out, and_2_out, and_3_out, and_4_out, and_5_out, and_6_out, and_7_out, and_8_out, and_9_out,
       and_10_out, and_11_out, and_12_out, and_13_out, and_14_out, and_15_out, and_16_out, and_17_out,
       and_18_out, and_25_out, and_26_out, decoder_1_out0, decoder_1_out1, decoder_1_out2, decoder_1_out3,
       decoder_1_out4, decoder_1_out5, decoder_1_out6, decoder_2_out4, decoder_2_out5, decoder_2_out6,
       decoder_2_out7, decoder_2_out8, decoder_2_out9, decoder_3_out0, decoder_3_out1, decoder_3_out2,
       or_1_out, or_2_out, or_3_out, or_4_out, or_5_out, or_6_out, or_7_out, or_8_out;

  Decoder #(.select(4)) decoder_1 (
    .out0(decoder_1_out0), .out1(decoder_1_out1), .out2(decoder_1_out2), .out3(decoder_1_out3),
    .out4(decoder_1_out4), .out5(decoder_1_out5), .out6(decoder_1_out6), .sel(Instruction));  // open: out7, out8, out9, out10, out11, out12, out13, out14, out15, en
  Decoder #(.select(4)) decoder_2 (
    .out4(decoder_2_out4), .out5(decoder_2_out5), .out6(decoder_2_out6), .out7(decoder_2_out7),
    .out8(decoder_2_out8), .out9(decoder_2_out9), .sel(count));  // open: out0, out1, out2, out3, out10, out11, out12, out13, out14, out15, en
  Decoder #(.select(2)) decoder_3 (
    .out0(decoder_3_out0), .out1(decoder_3_out1), .out2(decoder_3_out2), .sel(Mode));  // open: out3, en
  or or_1 (or_1_out, decoder_1_out4, decoder_1_out5, decoder_1_out6);
  or or_2 (or_2_out, decoder_1_out0, decoder_1_out1, decoder_1_out2, decoder_1_out3);
  and and_1 (and_1_out, decoder_3_out0, decoder_2_out5);
  and and_2 (and_2_out, decoder_3_out2, decoder_2_out5);
  and and_3 (and_3_out, decoder_3_out2, decoder_2_out7);
  and and_4 (and_4_out, decoder_3_out0, decoder_2_out6);
  and and_5 (and_5_out, decoder_3_out0, decoder_2_out7);
  and and_6 (and_6_out, decoder_3_out1, decoder_2_out5);
  and and_7 (and_7_out, decoder_3_out1, decoder_2_out6);
  and and_8 (and_8_out, decoder_3_out2, decoder_2_out8);
  and and_9 (and_9_out, decoder_3_out2, decoder_2_out9);
  or or_3 (or_3_out, decoder_1_out0, decoder_1_out1, decoder_1_out5, decoder_1_out6);
  or or_4 (or_4_out, and_1_out, and_2_out, and_3_out);
  and and_10 (and_10_out, decoder_3_out1, decoder_2_out4);
  and and_11 (and_11_out, decoder_3_out0, decoder_2_out5);
  and and_12 (and_12_out, decoder_3_out1, decoder_2_out4);
  and and_13 (and_13_out, decoder_3_out2, decoder_2_out6);
  or or_5 (or_5_out, and_4_out, and_5_out, and_6_out, and_7_out, and_8_out, and_9_out);
  or or_6 (or_6_out, and_11_out, and_12_out, and_13_out);
  and and_14 (and_14_out, decoder_3_out0, decoder_2_out6);
  and and_15 (and_15_out, decoder_3_out1, decoder_2_out5);
  and and_16 (and_16_out, decoder_3_out2, decoder_2_out8);
  or or_7 (or_7_out, and_14_out, and_15_out, and_16_out);
  or or_8 (or_8_out, decoder_3_out2, decoder_3_out0);
  and and_17 (and_17_out, or_1_out, decoder_3_out0, decoder_2_out5);
  or or_9 (Load_AC_from_ALU, and_17_out, and_18_out);
  and and_18 (and_18_out, or_2_out, or_7_out);
  and and_19 (Select_ADD, decoder_1_out0, or_5_out);
  and and_20 (Select_Subtract, decoder_1_out1, or_5_out);
  and and_21 (Select_AND, decoder_1_out2, or_5_out);
  and and_22 (Select_OR, decoder_1_out3, or_5_out);
  and and_23 (Load_Y_from_Mem_for_BinOp, or_4_out, or_2_out);
  and and_24 (Loady_Y_from_IR, and_10_out, or_2_out);
  and and_25 (and_25_out, or_6_out, or_2_out);
  or or_10 (Load_X_from_AC, and_25_out, and_26_out);
  and and_26 (and_26_out, decoder_3_out0, decoder_2_out4, or_1_out);
  and and_27 (Load_Flag_from_ALU, or_3_out, Load_AC_from_ALU);
  and and_28 (Load_ADDR_from_Y_for_BinOp, or_2_out, decoder_3_out2, decoder_2_out6);
  and and_29 (Load_ADDR_from_IR_for_BinOp, or_2_out, decoder_2_out5, or_8_out);

  // Notes on the sheet:
  //   Unary Operator
  //   Binary Operator
  //   Operator with flag
endmodule

module Control_for_Sto_Lod (
  input  [3:0] count,
  input  [3:0] Instruction,
  input  [1:0] Mode,
  output Load_Y_from_Mem_for_Sto_Lod,
  output Load_ADDR_from_Y_for_Sto_Lod,
  output Load_ADDR_from_IR_for_Sto_Lod
);

  wire decoder_1_out9, decoder_1_out10, decoder_2_out4, decoder_2_out5, decoder_2_out6, decoder_3_out0,
       decoder_3_out2, or_1_out, or_2_out;

  Decoder #(.select(4)) decoder_1 (
    .out9(decoder_1_out9), .out10(decoder_1_out10), .sel(Instruction));  // open: out0, out1, out2, out3, out4, out5, out6, out7, out8, out11, out12, out13, out14, out15, en
  Decoder #(.select(4)) decoder_2 (
    .out4(decoder_2_out4), .out5(decoder_2_out5), .out6(decoder_2_out6), .sel(count));  // open: out0, out1, out2, out3, out7, out8, out9, out10, out11, out12, out13, out14, out15, en
  Decoder #(.select(2)) decoder_3 (.out0(decoder_3_out0), .out2(decoder_3_out2), .sel(Mode));  // open: out1, out3, en
  or or_1 (or_1_out, decoder_1_out9, decoder_1_out10);
  or or_2 (or_2_out, decoder_3_out0, decoder_3_out2);
  and and_1 (Load_Y_from_Mem_for_Sto_Lod, or_1_out, decoder_2_out5, decoder_3_out2);
  and and_2 (Load_ADDR_from_Y_for_Sto_Lod, or_1_out, decoder_2_out6, decoder_3_out2);
  and and_3 (Load_ADDR_from_IR_for_Sto_Lod, or_1_out, or_2_out, decoder_2_out4);

  // Notes on the sheet:
  //   Lod
  //   Sto
endmodule

module Control_for_Count_0 (
  input  [3:0] count,
  input  [3:0] Instruction,
  input  [1:0] Mode,
  output Set_Count_to_Zero
);

  wire and_1_out, and_2_out, and_3_out, and_4_out, and_5_out, and_6_out, and_7_out, and_8_out, and_9_out,
       and_10_out, and_11_out, and_12_out, and_13_out, and_14_out, decoder_1_out0, decoder_1_out1,
       decoder_1_out2, decoder_1_out3, decoder_1_out4, decoder_1_out5, decoder_1_out6, decoder_1_out7,
       decoder_1_out8, decoder_1_out9, decoder_1_out10, decoder_1_out11, decoder_1_out12, decoder_1_out13,
       decoder_1_out14, decoder_1_out15, decoder_2_out4, decoder_2_out5, decoder_2_out6, decoder_2_out7,
       decoder_2_out8, decoder_2_out10, decoder_3_out0, decoder_3_out1, decoder_3_out2, decoder_3_out3,
       not_1_out, not_2_out, not_3_out, or_1_out, or_2_out, or_3_out, or_4_out, or_5_out, or_6_out, or_7_out,
       or_8_out, or_9_out, or_10_out, or_11_out;

  Decoder #(.select(4)) decoder_1 (
    .out0(decoder_1_out0), .out1(decoder_1_out1), .out2(decoder_1_out2), .out3(decoder_1_out3),
    .out4(decoder_1_out4), .out5(decoder_1_out5), .out6(decoder_1_out6), .out7(decoder_1_out7),
    .out8(decoder_1_out8), .out9(decoder_1_out9), .out10(decoder_1_out10), .out11(decoder_1_out11),
    .out12(decoder_1_out12), .out13(decoder_1_out13), .out14(decoder_1_out14), .out15(decoder_1_out15),
    .sel(Instruction));  // open: en
  Decoder #(.select(4)) decoder_2 (
    .out4(decoder_2_out4), .out5(decoder_2_out5), .out6(decoder_2_out6), .out7(decoder_2_out7),
    .out8(decoder_2_out8), .out10(decoder_2_out10), .sel(count));  // open: out0, out1, out2, out3, out9, out11, out12, out13, out14, out15, en
  Decoder #(.select(2)) decoder_3 (
    .out0(decoder_3_out0), .out1(decoder_3_out1), .out2(decoder_3_out2), .out3(decoder_3_out3), .sel(Mode));  // open: en
  or or_1 (or_1_out, decoder_1_out0, decoder_1_out1, decoder_1_out2, decoder_1_out3);
  or or_2 (or_2_out, decoder_1_out12, decoder_1_out13, decoder_1_out14, decoder_1_out15);
  or or_3 (or_3_out, decoder_1_out4, decoder_1_out5, decoder_1_out6);
  not not_1 (not_1_out, or_1_out);
  not not_2 (not_2_out, decoder_1_out9);
  or or_4 (or_4_out, decoder_1_out7, decoder_1_out8);
  and and_1 (and_1_out, not_1_out, not_2_out, decoder_3_out1);
  and and_2 (and_2_out, not_3_out, decoder_3_out2);
  or or_5 (or_5_out, decoder_1_out9, decoder_1_out10);
  not not_3 (not_3_out, or_6_out);
  or or_6 (or_6_out, or_1_out, or_5_out, or_2_out);
  or or_7 (or_7_out, and_1_out, and_2_out, decoder_3_out3);
  and and_3 (and_3_out, or_7_out, decoder_2_out4);
  and and_4 (and_4_out, decoder_1_out9, decoder_3_out1, decoder_2_out5);
  and and_5 (and_5_out, decoder_1_out11, decoder_2_out5);
  and and_6 (and_6_out, or_2_out, decoder_3_out0, decoder_2_out5);
  and and_7 (and_7_out, or_4_out, decoder_3_out0, decoder_2_out5);
  and and_8 (and_8_out, or_5_out, decoder_3_out0, decoder_2_out6);
  or or_8 (or_8_out, and_8_out, and_9_out);
  and and_9 (and_9_out, or_2_out, decoder_3_out2, decoder_2_out6);
  and and_10 (and_10_out, or_1_out, decoder_3_out1, decoder_2_out7);
  or or_9 (or_9_out, and_10_out, and_11_out);
  and and_11 (and_11_out, or_3_out, decoder_3_out2, decoder_2_out7);
  and and_12 (and_12_out, or_1_out, decoder_3_out0, decoder_2_out8);
  or or_10 (or_10_out, and_12_out, and_13_out);
  and and_13 (and_13_out, or_5_out, decoder_2_out8, decoder_3_out2);
  or or_11 (or_11_out, and_4_out, and_5_out, and_6_out, and_7_out);
  and and_14 (and_14_out, or_1_out, decoder_2_out10, decoder_3_out2);
  or or_12 (Set_Count_to_Zero, and_3_out, or_11_out, or_8_out, or_9_out, or_10_out, and_14_out);

  // Notes on the sheet:
  //   Binary Op
  //   Jump
  //   Halt
  //   Unary Op
  //   Sto
  //   Inc/Dec
  //   Lod
endmodule
